# Fritzing sketch pwm (saved by Fritzing 0.9.3b)
breadboards: 1

parts:
  Componente1 = Arduino Uno (Rev3)
  R1 = Resistor [tolerance=±5% resistance=220 package=THT]
  C1 = Tantalum Capacitor [capacitance=1μF package="100 mil [THT, tantalum]"]

nets:
  N1: Componente1.D11_PWM/MOSI, R1.Pin_1
  N2: Componente1.GND, C1.-
  N3: R1.Pin_0, C1.+
