# Fritzing sketch button_pin (saved by Fritzing 0.9.3b)
breadboards: 1

parts:
  Componente1 = Arduino Uno (Rev3)
  S1 = Pushbutton [package="[THT]"]
  R1 = Resistor [tolerance=±5% resistance=220 package=THT]
  C1 = Tantalum Capacitor [capacitance=1μF package="100 mil [THT, tantalum]"]
  R2 = Resistor [tolerance=±5% resistance=220 package=THT]

nets:
  N1: Componente1.D11_PWM/MOSI, R1.Pin_0
  N2: Componente1.D2, S1.Pin_1, S1.Pin_2, R2.Pin_0
  N3: Componente1.5V, S1.Pin_3, S1.Pin_4
  N4: Componente1.GND, C1.+, R2.Pin_1
  N5: R1.Pin_1, C1.-
