# Fritzing sketch conexion_motor_driver (saved by Fritzing 0.9.3b)
breadboards: 1

parts:
  Raspberry_Pi_1 = Raspberry Pi 3 [part_number=RPI-3-V1.2]
  U1 = L298_BRIDGE_DRIVER [package=powerso20]
  M1 = DC Motor
  VCC1 = Battery

nets:
  N1: Raspberry_Pi_1.GIPO12, U1.ENA
  N2: Raspberry_Pi_1.GIPO25, U1.IN2
  GND: Raspberry_Pi_1.GND, U1.GND, VCC1.-
  N3: Raspberry_Pi_1.GIPO23, U1.IN1
  N4: U1.OUT1, M1.pin_2
  N5: U1.OUT2, M1.pin_1
  N6: U1.VS, VCC1.+
