# Fritzing sketch circuito_2 (saved by Fritzing 0.9.3b)
breadboards: 1

parts:
  Raspberry_Pi_1 = Raspberry Pi 3 [part_number=RPI-3-V1.2]
  R1 = Resistor [tolerance=±5% resistance=220 package=THT]
  LED1 = LED - 5mm [color="Red (633nm)" package="5 mm [THT]"]
  LED2 = LED - 5mm [color="Red (633nm)" package="5 mm [THT]"]

nets:
  N1: Raspberry_Pi_1.GND, LED2.anode
  N2: Raspberry_Pi_1.5V, R1.Pin_0
  N3: R1.Pin_1, LED1.cathode
  N4: LED1.anode, LED2.cathode
