# Fritzing sketch circuito_3 (saved by Fritzing 0.9.3b)
breadboards: 1

parts:
  Raspberry_Pi_1 = Raspberry Pi 3 [part_number=RPI-3-V1.2]
  R1 = Resistor [tolerance=±5% resistance=220 package=THT]
  R2 = Resistor [tolerance=±5% resistance=220 package=THT]
  R3 = Resistor [tolerance=±5% resistance=220 package=THT]
  LED1 = LED - 5mm [color="Red (633nm)" package="5 mm [THT]"]

nets:
  N1: Raspberry_Pi_1.GND, LED1.cathode
  N2: Raspberry_Pi_1.5V, R1.Pin_0, R3.Pin_0
  N3: R1.Pin_1, R2.Pin_0
  N4: R2.Pin_1, R3.Pin_1, LED1.anode
