# Fritzing sketch circuito_5 (saved by Fritzing 0.9.3b)
breadboards: 1

parts:
  Raspberry_Pi_1 = Raspberry Pi 3 [part_number=RPI-3-V1.2]
  R1 = Resistor [tolerance=±5% resistance=220 package=THT]
  R2 = Resistor [tolerance=±5% resistance=220 package=THT]
  R3 = Resistor [tolerance=±5% resistance=220 package=THT]
  R4 = Resistor [tolerance=±5% resistance=220 package=THT]
  R5 = Resistor [tolerance=±5% resistance=220 package=THT]
  R6 = Resistor [tolerance=±5% resistance=220 package=THT]
  LED1 = LED - 5mm [color="Red (633nm)" package="5 mm [THT]"]
  LED2 = smd LED [color="Red (633nm)" package="0603 [SMD]"]  # not connected
  LED2_2 = smd LED [color="Red (633nm)" package="0805 [SMD]"]

nets:
  N1: Raspberry_Pi_1.GND, LED1.cathode, LED2_2.cathode
  N2: Raspberry_Pi_1.GPIO18, R4.Pin_1, R5.Pin_1, R6.Pin_1
  N3: Raspberry_Pi_1.GPIO15, R1.Pin_0, R2.Pin_0, R3.Pin_0
  N4: R1.Pin_1, R2.Pin_1, R3.Pin_1, LED1.anode
  N5: R4.Pin_0, R5.Pin_0, R6.Pin_0, LED2_2.anode
