# Fritzing sketch manual_motor_control_circuit (saved by Fritzing 0.9.3b)
breadboards: 1

parts:
  VCC1 = 4 x AAA Battery Mount
  M2 = DC Motor
  S1 = Pushbutton [package="[SMD]"]
  S2 = Pushbutton [package="[SMD]"]
  S3 = Pushbutton [package="[SMD]"]
  S4 = Pushbutton [package="[SMD]"]

nets:
  N1: VCC1.-, M2.pin_1, S1.Pin_1, S1.Pin_2, S2.Pin_3, S2.Pin_4, S3.Pin_3, S3.Pin_4
  N2: VCC1.+, S1.Pin_3, S1.Pin_4, S4.Pin_3, S4.Pin_4
  N3: M2.pin_2, S2.Pin_1, S2.Pin_2, S4.Pin_1, S4.Pin_2
  N4: S3.Pin_1, S3.Pin_2
